// Logisim project control_logic.circ as structural Verilog: 1 circuit, main circuit control_logic
module control_logic (
  input  [31:0] inst,
  input  BrEq,
  input  BrLt,
  output PCSel,
  output RegWEn,
  output [2:0] ImmSel,
  output BrUn,
  output ASel,
  output BSel,
  output [3:0] ALUSel,
  output MemRW,
  output [1:0] WBSel
);

  wire and_1_out, and_2_out, and_3_out, and_4_out, and_5_out, and_6_out, and_7_out, func3_is_0, func3_is_1,
       func3_is_2, func3_is_3, func3_is_4, func3_is_5, func3_is_6, func3_is_7, func7_is_00, func7_is_01,
       func7_is_20, is_I_format, is_I_format_jalr, is_I_format_lblhlw, is_R_format, is_S_format,
       is_SB_format, is_UJ_format;
  wire [2:0] demultiplexer_1_out1;
  wire [6:0] demultiplexer_2_out1;

  Comparator #(.width(7), .mode("unsigned")) comparator_1 (
    .a(inst[6:0]), .b(7'b1100011), .eq(is_SB_format));  // open: gt, lt
  Comparator #(.width(7), .mode("unsigned")) comparator_2 (
    .a(inst[6:0]), .b(7'b1100111), .eq(is_I_format_jalr));  // open: gt, lt
  Comparator #(.width(7), .mode("unsigned")) comparator_3 (
    .a(inst[6:0]), .b(7'b1101111), .eq(is_UJ_format));  // open: gt, lt
  Comparator #(.width(7), .mode("unsigned")) comparator_4 (
    .a(inst[6:0]), .b(7'b0110011), .eq(is_R_format));  // open: gt, lt
  Comparator #(.width(7), .mode("unsigned")) comparator_5 (
    .a(inst[6:0]), .b(7'b0000011), .eq(is_I_format_lblhlw));  // open: gt, lt
  Comparator #(.width(7), .mode("unsigned")) comparator_6 (
    .a(inst[6:0]), .b(7'b0010011), .eq(is_I_format));  // open: gt, lt
  Comparator #(.width(7), .mode("unsigned")) comparator_7 (
    .a(inst[6:0]), .b(7'b0100011), .eq(is_S_format));  // open: gt, lt
  or or_1 (PCSel, is_SB_format, is_I_format_jalr, is_UJ_format);
  Demultiplexer #(.width(3), .enable("false")) demultiplexer_1 (
    .out1(demultiplexer_1_out1), .in(inst[14:12]), .sel(is_R_format));  // open: out0
  Demultiplexer #(.width(7), .enable("false")) demultiplexer_2 (
    .out1(demultiplexer_2_out1), .in(inst[31:25]), .sel(is_R_format));  // open: out0
  Comparator #(.width(3), .mode("unsigned")) comparator_8 (
    .a(demultiplexer_1_out1), .b(3'b000), .eq(func3_is_0));  // open: gt, lt
  Comparator #(.width(3), .mode("unsigned")) comparator_9 (
    .a(demultiplexer_1_out1), .b(3'b001), .eq(func3_is_1));  // open: gt, lt
  Comparator #(.width(3), .mode("unsigned")) comparator_10 (
    .a(demultiplexer_1_out1), .b(3'b010), .eq(func3_is_2));  // open: gt, lt
  Comparator #(.width(3), .mode("unsigned")) comparator_11 (
    .a(demultiplexer_1_out1), .b(3'b011), .eq(func3_is_3));  // open: gt, lt
  Comparator #(.width(3), .mode("unsigned")) comparator_12 (
    .a(demultiplexer_1_out1), .b(3'b100), .eq(func3_is_4));  // open: gt, lt
  Comparator #(.width(3), .mode("unsigned")) comparator_13 (
    .a(demultiplexer_1_out1), .b(3'b101), .eq(func3_is_5));  // open: gt, lt
  Comparator #(.width(3), .mode("unsigned")) comparator_14 (
    .a(demultiplexer_1_out1), .b(3'b110), .eq(func3_is_6));  // open: gt, lt
  Comparator #(.width(3), .mode("unsigned")) comparator_15 (
    .a(demultiplexer_1_out1), .b(3'b111), .eq(func3_is_7));  // open: gt, lt
  Comparator #(.width(7), .mode("unsigned")) comparator_16 (
    .a(demultiplexer_2_out1), .b({7{1'b0}}), .eq(func7_is_00));  // open: gt, lt
  Comparator #(.width(7), .mode("unsigned")) comparator_17 (
    .a(demultiplexer_2_out1), .b(7'b0000001), .eq(func7_is_01));  // open: gt, lt
  Comparator #(.width(7), .mode("unsigned")) comparator_18 (
    .a(demultiplexer_2_out1), .b(7'b0100000), .eq(func7_is_20));  // open: gt, lt
  Demultiplexer #(.width(4), .enable("false")) demultiplexer_3 (
    .out1(ALUSel), .in(4'b0000), .sel(and_1_out));  // open: out0
  and and_1 (and_1_out, func3_is_0, func7_is_00);
  Demultiplexer #(.width(4), .enable("false")) demultiplexer_4 (
    .out1(ALUSel), .in(4'b1010), .sel(and_2_out));  // open: out0
  and and_2 (and_2_out, func3_is_0, func7_is_01);
  Demultiplexer #(.width(4), .enable("false")) demultiplexer_5 (
    .out1(ALUSel), .in(4'b1100), .sel(and_3_out));  // open: out0
  and and_3 (and_3_out, func3_is_0, func7_is_20);
  Demultiplexer #(.width(4), .enable("false")) demultiplexer_6 (
    .out1(ALUSel), .in(4'b0110), .sel(and_4_out));  // open: out0
  and and_4 (and_4_out, func3_is_1, func7_is_00);
  Demultiplexer #(.width(4), .enable("false")) demultiplexer_7 (
    .out1(ALUSel), .in(4'b1110), .sel(and_5_out));  // open: out0
  and and_5 (and_5_out, func3_is_1, func7_is_01);
  Demultiplexer #(.width(4), .enable("false")) demultiplexer_8 (
    .out1(ALUSel), .in(4'b1011), .sel(and_6_out));  // open: out0
  and and_6 (and_6_out, func3_is_3, func7_is_00);
  Demultiplexer #(.width(4), .enable("false")) demultiplexer_9 (
    .out1(ALUSel), .in(4'b0111), .sel(and_7_out));  // open: out0
  and and_7 (and_7_out, func3_is_2, func7_is_00);

  // Other names for the same wires on the sheet: opcode[6:0] = inst[6:0]; func3[2:0] = inst[14:12];
  //   func7[6:0] = inst[31:25]

  // Notes on the sheet:
  //   INPUTS to your circuit
  //   DON'T CHANGE THE LOCATIONS OF THE INPUTS AND OUTPUTS!
  //   OUTPUT from your circuit
endmodule
