// Logisim project cpu.circ as structural Verilog: 1 circuit, main circuit main
module main (
  input  [31:0] INSTRUCTION,
  input  CLOCK,
  output [31:0] PROGRAM_COUNTER,
  output [31:0] ra,
  output [31:0] sp,
  output [31:0] t0,
  output [31:0] t1,
  output [31:0] t2,
  output [31:0] s0,
  output [31:0] s1,
  output [31:0] a0
);

  wire control_logic_1_regwen, undriven_3;
  wire [1:0] control_logic_1_wbsel;
  wire [2:0] control_logic_1_immsel, undriven;
  wire [31:0] adder_1_out, Arithmetic_Logic_Unit_result, imm_output, rs1_output, undriven_2;

  Adder #(.width(32)) adder_1 (.a(PROGRAM_COUNTER), .b(32'h4), .out(adder_1_out));  // open: cin, cout
  Register #(.width(32)) PC (.D(adder_1_out), .clk(CLOCK), .Q(PROGRAM_COUNTER));  // open: en, clr
  control_logic control_logic_1 (
    .ImmSel(control_logic_1_immsel), .RegWEn(control_logic_1_regwen), .WBSel(control_logic_1_wbsel));  // open: BSel, ASel, BrUn, PCSel, BrLt, BrEq, inst, ALUSel, MemRW
  imm_gen imm_gen_1 (.ImmSel(undriven), .imm(imm_output), .inst(INSTRUCTION));
  regfile_main RegFile (
    .rd(INSTRUCTION[11:7]), .Read_Data_1(rs1_output), .ra(ra), .sp(sp), .t0(t0), .t1(t1), .t2(t2), .s0(s0),
    .s1(s1), .a0(a0), .rs1(INSTRUCTION[19:15]), .Write_Data(undriven_2), .RegWEn(undriven_3), .clk(CLOCK));  // open: rs2, Read_Data_2
  alu Arithmetic_Logic_Unit (.ALUSel(4'b0000), .Result(Arithmetic_Logic_Unit_result), .A(rs1_output), .B(imm_output));
  // branch_comp branch_comp_1: pin names not known
  // mem_main DMEM: pin names not known; wires that end beside it: CLOCK

  // Other names for the same wires on the sheet: clk = CLOCK; fetch_addr[31:0] = PROGRAM_COUNTER;
  //   opcode[6:0] = INSTRUCTION[6:0]; rd[4:0] = INSTRUCTION[11:7]; func3[2:0] = INSTRUCTION[14:12];
  //   rs1[4:0] = INSTRUCTION[19:15]; imm[11:0] = INSTRUCTION[31:20]

  // Notes on the sheet:
  //   from run.circ
  //   Output
  //   IF Stage
  //   from run.circ
  //   IMEM (do **NOT** move this)
  //   Inputs
  //   ID Stage
  //   for addi (I format)
  //   It is OK to move the PC, RegFile, ALU, MEM, Branch Comp, Imm Gen, and Control Logic to wherever is most convenient for you when constructing your CPU, and to delete this text
  //   Inputs/Outputs for testing. Do **NOT** move these.
endmodule
